// Logisim project Estudo Frequencia.circ as structural Verilog
module Ficha_06_Ex_1 (
  input  A,
  input  B,
  input  Ci,
  output S,
  output Co
);

  wire and_1_out, and_2_out, xor_1_out;

  xor xor_1 (xor_1_out, A, B);
  and and_1 (and_1_out, A, B);
  xor xor_2 (S, xor_1_out, Ci);
  and and_2 (and_2_out, xor_1_out, Ci);
  or or_1 (Co, and_1_out, and_2_out);

  // Notes on the sheet:
  //   S=A xor B xor C
  //   Co=AB+Ci(A xor B)
  //   SOMADOR DE 1 BIT
endmodule

module Somador_4_bits (
  input  B1,
  input  A1,
  input  B2,
  input  A2,
  input  B3,
  input  A3,
  input  B4,
  input  A4,
  input  C0,
  output C4,
  output S1,
  output S2,
  output S3,
  output S4
);

  wire ficha_06_ex_1_1_co, ficha_06_ex_1_2_co, ficha_06_ex_1_3_co;

  Ficha_06_Ex_1 ficha_06_ex_1_1 (.A(A1), .B(B1), .Ci(C0), .S(S1), .Co(ficha_06_ex_1_1_co));
  Ficha_06_Ex_1 ficha_06_ex_1_2 (.A(A2), .B(B2), .Ci(ficha_06_ex_1_1_co), .S(S2), .Co(ficha_06_ex_1_2_co));
  Ficha_06_Ex_1 ficha_06_ex_1_3 (.A(A3), .B(B3), .Ci(ficha_06_ex_1_2_co), .S(S3), .Co(ficha_06_ex_1_3_co));
  Ficha_06_Ex_1 ficha_06_ex_1_4 (.A(A4), .B(B4), .Ci(ficha_06_ex_1_3_co), .S(S4), .Co(C4));

  // Notes on the sheet:
  //   SOMADOR DE 4BITS
endmodule

module Ficha_06_Ex_2 (
  input  Xn1,
  input  Yn1,
  input  A,
  input  B,
  output Xn,
  output Yn
);

  wire and_1_out, and_2_out, not_1_out, not_2_out, not_3_out, not_4_out;

  not not_1 (not_1_out, Yn1);
  not not_2 (not_2_out, B);
  not not_3 (not_3_out, Xn1);
  not not_4 (not_4_out, A);
  and and_1 (and_1_out, not_1_out, A, not_2_out);
  and and_2 (and_2_out, not_3_out, not_4_out, B);
  or or_1 (Xn, and_1_out, Xn1);
  or or_2 (Yn, and_2_out, Yn1);

  // Notes on the sheet:
  //   COMPARADOR DE 1 BIT
endmodule

module Comparador_de_4_bits (
  input  Xn1,
  input  Yn1,
  input  A1,
  input  A2,
  input  B2,
  input  A3,
  input  B3,
  input  A4,
  input  B4,
  input  B1,
  output Xn,
  output Yn
);

  wire ficha_06_ex_2_1_xn, ficha_06_ex_2_1_yn, ficha_06_ex_2_2_xn, ficha_06_ex_2_2_yn, ficha_06_ex_2_3_xn,
       ficha_06_ex_2_3_yn;

  Ficha_06_Ex_2 ficha_06_ex_2_1 (
    .Xn1(Xn1), .Yn1(Yn1), .A(A1), .B(B1), .Xn(ficha_06_ex_2_1_xn), .Yn(ficha_06_ex_2_1_yn));
  Ficha_06_Ex_2 ficha_06_ex_2_2 (
    .Xn1(ficha_06_ex_2_1_xn), .Yn1(ficha_06_ex_2_1_yn), .A(A2), .B(B2), .Xn(ficha_06_ex_2_2_xn),
    .Yn(ficha_06_ex_2_2_yn));
  Ficha_06_Ex_2 ficha_06_ex_2_3 (
    .Xn1(ficha_06_ex_2_2_xn), .Yn1(ficha_06_ex_2_2_yn), .A(A3), .B(B3), .Xn(ficha_06_ex_2_3_xn),
    .Yn(ficha_06_ex_2_3_yn));
  Ficha_06_Ex_2 ficha_06_ex_2_4 (.Xn1(ficha_06_ex_2_3_xn), .Yn1(ficha_06_ex_2_3_yn), .A(A4), .B(B4), .Xn(Xn), .Yn(Yn));

  // Notes on the sheet:
  //   COMPARADOR DE 4BITS
endmodule

module Descodificador_de_3bits (
  input  A,
  input  B,
  input  C,
  output _0,
  output _1,
  output _2,
  output _3,
  output _4,
  output _5,
  output _6,
  output _7
);

  wire not_1_out, not_2_out, not_3_out;

  not not_1 (not_1_out, A);
  not not_2 (not_2_out, B);
  not not_3 (not_3_out, C);
  and and_1 (_0, not_3_out, not_2_out, not_1_out);
  and and_2 (_1, C, not_2_out, not_1_out);
  and and_3 (_2, not_3_out, B, not_1_out);
  and and_4 (_3, C, B, not_1_out);
  and and_5 (_4, not_3_out, not_2_out, A);
  and and_6 (_5, C, not_2_out, A);
  and and_7 (_6, not_3_out, B, A);
  and and_8 (_7, C, B, A);

  // Notes on the sheet:
  //   DESCODIFICADOR DE 3BITS
endmodule

module Ficha_06_Ex_5 (
  input  in_1,
  input  in_2,
  input  in_3,
  input  in_4,
  output _0,
  output _1,
  output _2,
  output _3,
  output _4,
  output _5
);

  wire not_1_out, not_2_out, not_3_out, not_4_out;

  not not_1 (not_1_out, in_1);
  not not_2 (not_2_out, in_2);
  not not_3 (not_3_out, in_3);
  not not_4 (not_4_out, in_4);
  and and_1 (_0, in_4, in_3, not_2_out, not_1_out);
  and and_2 (_1, in_4, not_3_out, in_2, not_1_out);
  and and_3 (_2, not_4_out, in_3, in_2, not_1_out);
  and and_4 (_3, in_4, not_3_out, not_2_out, in_1);
  and and_5 (_4, not_4_out, in_3, not_2_out, in_1);
  and and_6 (_5, not_4_out, not_3_out, in_2, in_1);
endmodule
