// Logisim project Trabalho SD.circ as structural Verilog: 4 circuits, main circuit DISPLAY
module DISPLAY (
  input  in_1,
  output S0,
  output S1,
  output S2,
  output S3,
  output S4,
  output S5,
  output S6
);

  wire and_1_out, and_2_out, and_3_out, and_4_out, and_5_out, and_6_out, and_7_out, and_8_out, and_9_out,
       clock_1_out, JK0_q, JK0_qn, JK1_q, JK1_qn, JK2_q, JK2_qn, xor_1_out, xor_2_out;

  Clock clock_1 (.out(clock_1_out));
  and and_1 (and_1_out, JK1_q, JK0_q);
  J_K_Flip_Flop JK0 (.J(in_1), .clk(clock_1_out), .K(in_1), .Q(JK0_q), .Qn(JK0_qn));  // open: preset, en, reset
  J_K_Flip_Flop JK1 (.J(JK0_q), .clk(clock_1_out), .K(JK0_q), .Q(JK1_q), .Qn(JK1_qn));  // open: preset, en, reset
  J_K_Flip_Flop JK2 (
    .J(and_1_out), .clk(clock_1_out), .K(and_1_out), .Q(JK2_q), .Qn(JK2_qn));  // open: preset, en, reset
  xor xor_1 (xor_1_out, JK1_q, JK0_q);
  and and_2 (and_2_out, JK0_qn, JK1_q);
  and and_3 (and_3_out, JK1_q, JK2_qn);
  and and_4 (and_4_out, JK0_qn, JK2_qn);
  and and_5 (and_5_out, JK0_q, JK1_qn, JK2_q);
  and and_6 (and_6_out, JK0_qn, JK1_q);
  and and_7 (and_7_out, JK0_qn, JK2_qn);
  and and_8 (and_8_out, JK1_q, JK2_qn);
  and and_9 (and_9_out, JK0_qn, JK1_qn);
  xor xor_2 (xor_2_out, JK2_q, JK1_q);
  or or_1 (S0, xor_1_out, JK2_qn);
  or or_2 (S1, JK2_q, JK1_qn);
  or or_3 (S2, JK0_q, JK2_qn, JK1_qn);
  or or_4 (S3, and_2_out, and_3_out, and_4_out, and_5_out);
  or or_5 (S4, and_6_out, and_7_out);
  or or_6 (S5, and_8_out, and_9_out);
  or or_7 (S6, xor_2_out, JK0_qn);
endmodule

module \CIRCUITOS_VEÍCULOS  (
  input  \Botão_Sensor ,
  input  EC,
  output VM,
  output AM,
  output VE
);

  wire and_1_out, clock_1_out, JK0_q, JK0_qn, JK1_q, JK1_qn, or_1_out, or_2_out;

  Clock clock_1 (.out(clock_1_out));
  or or_1 (or_1_out, JK1_q, \Botão_Sensor );
  or or_2 (or_2_out, EC, JK1_qn);
  and and_1 (and_1_out, EC, JK0_q);
  J_K_Flip_Flop JK0 (.J(or_1_out), .clk(clock_1_out), .K(or_2_out), .Q(JK0_q), .Qn(JK0_qn));  // open: preset, en, reset
  J_K_Flip_Flop JK1 (.J(JK0_q), .clk(clock_1_out), .K(and_1_out), .Q(JK1_q), .Qn(JK1_qn));  // open: preset, en, reset
  and and_2 (VM, JK1_q, JK0_q);
  and and_3 (VE, JK1_qn, JK0_qn);
  xor xor_1 (AM, JK1_q, JK0_q);
endmodule

module \CIRCUITO_PEÕS_COM_JK  (
  input  \Botão_OU_Sensor ,
  input  in_2,
  output VM,
  output AM,
  output VE,
  output EC
);

  wire and_1_out, and_2_out, and_3_out, and_4_out, and_5_out, and_6_out, and_7_out, and_8_out, and_9_out,
       and_10_out, and_11_out, and_12_out, and_13_out, and_14_out, and_15_out, and_16_out, and_17_out,
       and_18_out, and_19_out, and_20_out, and_21_out, and_22_out, and_23_out, and_24_out, and_25_out,
       and_26_out, and_27_out, and_28_out, and_29_out, and_30_out, and_31_out, and_32_out, and_33_out,
       and_34_out, clock_1_out, JK0_q, JK0_qn, JK1_q, JK1_qn, JK2_q, JK2_qn, JK3_q, JK3_qn, not_1_out,
       not_2_out, not_3_out, not_4_out, not_5_out, not_6_out, not_7_out, not_8_out, not_9_out, not_10_out,
       not_11_out, not_12_out, not_13_out, not_14_out, not_15_out, not_16_out, not_17_out, or_1_out,
       or_2_out, or_3_out, or_4_out, or_5_out, or_6_out, or_7_out;

  Clock clock_1 (.out(clock_1_out));
  and and_1 (and_1_out, \Botão_OU_Sensor , JK3_qn);
  and and_2 (and_2_out, \Botão_OU_Sensor , JK1_qn);
  and and_3 (and_3_out, \Botão_OU_Sensor , JK2_qn, JK3_q);
  not not_1 (not_1_out, \Botão_OU_Sensor );
  and and_4 (and_4_out, not_1_out, JK1_q, JK3_qn);
  not not_2 (not_2_out, \Botão_OU_Sensor );
  and and_5 (and_5_out, not_2_out, JK1_qn, JK2_q);
  not not_3 (not_3_out, \Botão_OU_Sensor );
  and and_6 (and_6_out, not_3_out, JK2_qn, JK3_q);
  not not_4 (not_4_out, \Botão_OU_Sensor );
  not not_5 (not_5_out, JK0_q);
  not not_6 (not_6_out, JK0_q);
  and and_7 (and_7_out, \Botão_OU_Sensor , JK1_q, JK3_q);
  and and_8 (and_8_out, \Botão_OU_Sensor , JK0_q, JK1_q);
  not not_7 (not_7_out, \Botão_OU_Sensor );
  and and_9 (and_9_out, not_7_out, JK1_q, JK3_q);
  not not_8 (not_8_out, \Botão_OU_Sensor );
  and and_10 (and_10_out, not_8_out, JK0_q, JK1_q);
  not not_9 (not_9_out, \Botão_OU_Sensor );
  and and_11 (and_11_out, \Botão_OU_Sensor , JK0_q);
  and and_12 (and_12_out, not_4_out, JK0_q);
  and and_13 (and_13_out, \Botão_OU_Sensor , JK2_q, JK3_q);
  and and_14 (and_14_out, \Botão_OU_Sensor , JK0_q);
  and and_15 (and_15_out, not_5_out, JK2_q, JK3_q);
  and and_16 (and_16_out, not_6_out, JK0_q);
  and and_17 (and_17_out, \Botão_OU_Sensor , JK0_q, JK1_q);
  not not_10 (not_10_out, \Botão_OU_Sensor );
  and and_18 (and_18_out, not_10_out, JK0_q, JK1_q);
  and and_19 (and_19_out, \Botão_OU_Sensor , JK0_q, JK1_q, JK2_q);
  and and_20 (and_20_out, not_9_out, JK0_q, JK1_q, JK2_q);
  and and_21 (and_21_out, \Botão_OU_Sensor , JK1_q, JK2_q);
  not not_11 (not_11_out, \Botão_OU_Sensor );
  and and_22 (and_22_out, not_11_out, JK1_q, JK2_q);
  or or_1 (or_1_out, and_1_out, and_2_out, and_3_out, and_4_out, and_5_out, and_6_out);
  or or_2 (or_2_out, and_11_out, and_12_out);
  or or_3 (or_3_out, and_13_out, and_14_out, and_15_out, and_16_out);
  or or_4 (or_4_out, and_17_out, and_18_out);
  or or_5 (or_5_out, and_7_out, and_8_out, and_9_out, and_10_out);
  or or_6 (or_6_out, and_19_out, and_20_out);
  or or_7 (or_7_out, and_21_out, and_22_out);
  J_K_Flip_Flop JK0 (.J(or_1_out), .clk(clock_1_out), .K(in_2), .Q(JK0_q), .Qn(JK0_qn));  // open: preset, en, reset
  J_K_Flip_Flop JK1 (.J(or_2_out), .clk(clock_1_out), .K(or_3_out), .Q(JK1_q), .Qn(JK1_qn));  // open: preset, en, reset
  J_K_Flip_Flop JK2 (.J(or_4_out), .clk(clock_1_out), .K(or_5_out), .Q(JK2_q), .Qn(JK2_qn));  // open: preset, en, reset
  J_K_Flip_Flop JK3 (.J(or_6_out), .clk(clock_1_out), .K(or_7_out), .Q(JK3_q), .Qn(JK3_qn));  // open: preset, en, reset
  not not_12 (not_12_out, \Botão_OU_Sensor );
  not not_13 (not_13_out, \Botão_OU_Sensor );
  not not_14 (not_14_out, \Botão_OU_Sensor );
  not not_15 (not_15_out, \Botão_OU_Sensor );
  and and_23 (and_23_out, \Botão_OU_Sensor , JK1_q, JK2_q, JK3_q);
  and and_24 (and_24_out, \Botão_OU_Sensor , JK2_qn, JK3_qn);
  and and_25 (and_25_out, not_12_out, JK1_q, JK2_q, JK3_q);
  not not_16 (not_16_out, \Botão_OU_Sensor );
  and and_26 (and_26_out, not_16_out, JK2_qn, JK3_qn);
  and and_27 (and_27_out, \Botão_OU_Sensor , JK1_qn, JK2_q, JK3_q);
  and and_28 (and_28_out, not_13_out, JK1_qn, JK2_q, JK3_q);
  and and_29 (and_29_out, \Botão_OU_Sensor , JK2_qn, JK3_q);
  and and_30 (and_30_out, \Botão_OU_Sensor , JK2_q, JK3_qn);
  not not_17 (not_17_out, \Botão_OU_Sensor );
  and and_31 (and_31_out, not_17_out, JK2_qn, JK3_q);
  and and_32 (and_32_out, not_14_out, JK2_q, JK3_qn);
  and and_33 (and_33_out, \Botão_OU_Sensor , JK1_q, JK2_q, JK3_q);
  and and_34 (and_34_out, not_15_out, JK1_q, JK2_q, JK3_q);
  or or_8 (EC, and_33_out, and_34_out);
  or or_9 (VM, and_23_out, and_24_out, and_25_out, and_26_out);
  or or_10 (AM, and_27_out, and_28_out);
  or or_11 (VE, and_29_out, and_30_out, and_31_out, and_32_out);
endmodule

module CIRCUITO_FINAL (
  input  in_1
);

  wire \circuito_peõs_com_jk_1_am , \circuito_peõs_com_jk_1_ec , \circuito_peõs_com_jk_1_ve ,
       \circuito_peõs_com_jk_1_vm , \circuitos_veículos_1_am , \circuitos_veículos_1_ve ,
       \circuitos_veículos_1_vm , display_1_s0, display_1_s1, display_1_s2, display_1_s3, display_1_s4,
       display_1_s5, display_1_s6;

  \CIRCUITOS_VEÍCULOS  \circuitos_veículos_1  (
    .\Botão_Sensor (in_1), .EC(\circuito_peõs_com_jk_1_ec ), .VM(\circuitos_veículos_1_vm ),
    .AM(\circuitos_veículos_1_am ), .VE(\circuitos_veículos_1_ve ));
  \CIRCUITO_PEÕS_COM_JK  \circuito_peõs_com_jk_1  (
    .in_2(in_1), .\Botão_OU_Sensor (in_1), .VM(\circuito_peõs_com_jk_1_vm ),
    .AM(\circuito_peõs_com_jk_1_am ), .VE(\circuito_peõs_com_jk_1_ve ), .EC(\circuito_peõs_com_jk_1_ec ));
  DISPLAY display_1 (
    .in_1(\circuito_peõs_com_jk_1_ve ), .S0(display_1_s0), .S1(display_1_s1), .S2(display_1_s2),
    .S3(display_1_s3), .S4(display_1_s4), .S5(display_1_s5), .S6(display_1_s6));
  LED \Veículos  (.in(\circuitos_veículos_1_vm ));
  LED led_1 (.in(\circuitos_veículos_1_am ));
  LED led_2 (.in(\circuitos_veículos_1_ve ));
  LED \Peões  (.in(\circuito_peõs_com_jk_1_vm ));
  LED led_3 (.in(\circuito_peõs_com_jk_1_am ));
  LED led_4 (.in(\circuito_peõs_com_jk_1_ve ));
  _7_Segment_Display u_7_segment_display_1 (
    .g(display_1_s6), .f(display_1_s5), .a(display_1_s0), .b(display_1_s1), .e(display_1_s4),
    .d(display_1_s3), .c(display_1_s2));  // open: dp

  // Notes on the sheet:
  //   Circuito dos Veículos
  //   Circuito dos Peões
  //   Circuito do Display
endmodule
