// Logisim project Implementação final.circ as structural Verilog: 2 circuits, main circuit main
module main (
  output \DCafé ,
  output BAgua,
  output BAgua2,
  output \DAçucar 
);

  wire and_1_out, and_2_out, and_3_out, and_4_out, and_5_out, and_6_out, and_7_out, and_8_out, and_9_out,
       and_10_out, and_11_out, and_12_out, B_out, clock_1_out, M1_out, M2_out, not_1_out, not_2_out,
       not_3_out, not_4_out, not_5_out, not_6_out, not_7_out, not_8_out, not_9_out, not_10_out, not_11_out,
       not_12_out, not_13_out, not_14_out, not_15_out, not_16_out, not_17_out, not_18_out, not_19_out,
       or_1_out, or_2_out, or_3_out, or_4_out, or_5_out, or_6_out, T1_2_q, T1_q, T2_2_q, T2_q, T3_q;

  Button M1 (.out(M1_out));
  Button M2 (.out(M2_out));
  not not_1 (not_1_out, T2_q);
  not not_2 (not_2_out, T1_q);
  not not_3 (not_3_out, T1_q);
  not not_4 (not_4_out, T2_q);
  not not_5 (not_5_out, T2_q);
  Clock clock_1 (.out(clock_1_out));
  and and_1 (and_1_out, M1_out, not_1_out);
  and and_2 (and_2_out, M1_out, not_2_out);
  and and_3 (and_3_out, M2_out, T2_q, not_3_out);
  and and_4 (and_4_out, and_12_out, T2_q, T1_q);
  and and_5 (and_5_out, M2_out, not_4_out);
  and and_6 (and_6_out, M1_out, not_5_out, T1_q);
  and and_7 (and_7_out, and_12_out, T2_q, T1_q);
  or or_1 (or_1_out, and_1_out, and_2_out, and_3_out, and_4_out);
  or or_2 (or_2_out, and_5_out, and_6_out, and_7_out);
  or or_3 (or_3_out, and_9_out, T3_q, T2_2_q, T1_2_q);
  and and_8 (and_8_out, T2_2_q, T1_2_q);
  T_Flip_Flop T1 (.clk(clock_1_out), .T(or_1_out), .Q(T1_q));  // open: Qn, preset, reset, en
  T_Flip_Flop T2 (.clk(clock_1_out), .T(or_2_out), .Q(T2_q));  // open: Qn, preset, reset, en
  T_Flip_Flop T2_2 (.clk(clock_1_out), .T(T1_2_q), .Q(T2_2_q));  // open: Qn, preset, reset, en
  Button B (.out(B_out));
  T_Flip_Flop T1_2 (.clk(clock_1_out), .T(or_3_out), .Q(T1_2_q));  // open: Qn, preset, reset, en
  T_Flip_Flop T3 (.clk(clock_1_out), .T(and_8_out), .Q(T3_q));  // open: Qn, preset, reset, en
  and and_9 (and_9_out, B_out, T1_q, T2_q);
  LED Dinheiro (.in(and_10_out));
  and and_10 (and_10_out, T2_q, T1_q);
  not not_6 (not_6_out, T1_q);
  not not_7 (not_7_out, T2_q);
  not not_8 (not_8_out, T1_q);
  not not_9 (not_9_out, T1_q);
  not not_10 (not_10_out, T2_q);
  not not_11 (not_11_out, T1_q);
  not not_12 (not_12_out, T2_2_q);
  not not_13 (not_13_out, T3_q);
  not not_14 (not_14_out, T2_2_q);
  not not_15 (not_15_out, T3_q);
  not not_16 (not_16_out, T1_2_q);
  not not_17 (not_17_out, T3_q);
  not not_18 (not_18_out, T2_2_q);
  not not_19 (not_19_out, T1_2_q);
  or or_4 (or_4_out, T2_q, not_6_out);
  or or_5 (or_5_out, not_7_out, T1_q);
  or or_6 (or_6_out, T2_q, not_8_out);
  and and_11 (and_11_out, not_10_out, not_11_out);
  and and_12 (and_12_out, T3_q, not_12_out, T1_2_q);
  and and_13 (\DCafé , not_13_out, not_14_out, T1_2_q);
  and and_14 (BAgua, not_15_out, T2_2_q, not_16_out);
  and and_15 (BAgua2, not_17_out, T2_2_q, T1_2_q);
  and and_16 (\DAçucar , T3_q, not_18_out, not_19_out);
  _7_Segment_Display u_7_segment_display_1 (
    .g(T2_q), .f(and_11_out), .a(or_4_out), .b(1'b1), .e(not_9_out), .d(or_6_out), .c(or_5_out));  // open: dp
  LED \Café_servido  (.in(and_12_out));
endmodule

module DISPLAY (
  input  K2,
  input  K1,
  input  K0,
  output CP,
  output DC,
  output BA1,
  output BA2,
  output DA
);

  wire not_1_out, not_2_out, not_3_out, not_4_out, not_5_out, not_6_out, not_7_out, not_8_out;

  not not_1 (not_1_out, K1);
  not not_2 (not_2_out, K2);
  not not_3 (not_3_out, K1);
  not not_4 (not_4_out, K2);
  not not_5 (not_5_out, K0);
  not not_6 (not_6_out, K2);
  not not_7 (not_7_out, K1);
  not not_8 (not_8_out, K0);
  and and_1 (CP, K2, not_1_out, K0);
  and and_2 (DC, not_2_out, not_3_out, K0);
  and and_3 (BA1, not_4_out, K1, not_5_out);
  and and_4 (BA2, not_6_out, K1, K0);
  and and_5 (DA, K2, not_7_out, not_8_out);
endmodule
